// Digital circuit desmultiplexador de palavras de 2 bit.dig as structural Verilog
module desmultiplexador_de_palavras_de_2_bit (
  input  B0,
  input  S0,
  input  S1,
  input  B1
);

  wire and_1_out, and_2_out, and_3_out, and_4_out, and_5_out, and_6_out, and_7_out, and_8_out, and_9_out,
       and_10_out, and_11_out, and_12_out, not_1_out, not_2_out, not_3_out, not_4_out;

  not not_1 (not_1_out, S0);
  not not_2 (not_2_out, S1);
  not not_3 (not_3_out, S0);
  not not_4 (not_4_out, S1);
  and and_1 (and_1_out, not_1_out, not_2_out);
  and and_2 (and_2_out, not_3_out, S1);
  and and_3 (and_3_out, S0, not_4_out);
  and and_4 (and_4_out, S0, S1);
  and and_5 (and_5_out, B0, and_1_out);
  and and_6 (and_6_out, and_1_out, B1);
  and and_7 (and_7_out, B0, and_2_out);
  and and_8 (and_8_out, and_2_out, B1);
  and and_9 (and_9_out, B0, and_3_out);
  and and_10 (and_10_out, and_3_out, B1);
  and and_11 (and_11_out, B0, and_4_out);
  and and_12 (and_12_out, and_4_out, B1);
  LED A0 (.in(and_5_out));
  LED A1 (.in(and_6_out));
  LED u_B0 (.in(and_7_out));
  LED u_B1 (.in(and_8_out));
  LED C0 (.in(and_9_out));
  LED C1 (.in(and_10_out));
  LED D0 (.in(and_11_out));
  LED D1 (.in(and_12_out));
endmodule
