// Digital circuit comador completo.dig as structural Verilog
module comador_completo (
  input  bitA,
  input  bitB,
  input  carryIn
);

  wire and_1_out, and_2_out, and_3_out, or_1_out, xor_1_out;

  and and_1 (and_1_out, bitA, bitB);
  and and_2 (and_2_out, carryIn, bitB);
  and and_3 (and_3_out, carryIn, bitA);
  xor xor_1 (xor_1_out, bitA, bitB, carryIn);
  or or_1 (or_1_out, and_1_out, and_2_out, and_3_out);
  LED sum (.in(xor_1_out));
  LED carryOut (.in(or_1_out));
endmodule
