// Digital circuit desmultiplexador de palavras de 2 bit de quatro saídas - portas logicas + cl.dig as structural Verilog
module \desmultiplexador_de_palavras_de_2_bit_de_quatro_saídas___portas_logicas___cl  (
  input  B0,
  input  S0,
  input  S1,
  input  B1,
  input  S0_2,
  input  S1_2,
  input  BIT0,
  input  BIT1
);

  wire _7404_1_pin2, _7404_1_pin4, _7408_1_pin3, _7408_1_pin6, _7408_1_pin8, _7408_1_pin10, _7408_2_pin3,
       _7408_2_pin6, _7408_2_pin8, _7408_2_pin10, _7408_3_pin3, _7408_3_pin6, _7408_3_pin8, _7408_3_pin10,
       _7408_4_pin3, _7408_4_pin6, _7408_4_pin8, _7408_4_pin10, and_1_out, and_2_out, and_3_out, and_4_out,
       and_5_out, and_6_out, and_7_out, and_8_out, and_9_out, and_10_out, and_11_out, and_12_out, not_1_out,
       not_2_out, not_3_out, not_4_out;

  not not_1 (not_1_out, S0);
  and and_1 (and_1_out, not_1_out, not_2_out);
  not not_2 (not_2_out, S1);
  not not_3 (not_3_out, S0);
  and and_2 (and_2_out, not_3_out, S1);
  and and_3 (and_3_out, S0, not_4_out);
  not not_4 (not_4_out, S1);
  and and_4 (and_4_out, S0, S1);
  and and_5 (and_5_out, B0, and_1_out);
  and and_6 (and_6_out, and_1_out, B1);
  and and_7 (and_7_out, B0, and_2_out);
  and and_8 (and_8_out, and_2_out, B1);
  and and_9 (and_9_out, B0, and_3_out);
  and and_10 (and_10_out, and_3_out, B1);
  and and_11 (and_11_out, B0, and_4_out);
  and and_12 (and_12_out, and_4_out, B1);
  LED A0 (.in(and_5_out));
  LED A1 (.in(and_6_out));
  LED u_B0 (.in(and_7_out));
  LED u_B1 (.in(and_8_out));
  LED C0 (.in(and_9_out));
  LED C1 (.in(and_10_out));
  LED D0 (.in(and_11_out));
  LED D1 (.in(and_12_out));
  _7404 _7404_1 (
    .pin1(S0_2), .pin2(_7404_1_pin2), .pin3(S1_2), .pin4(_7404_1_pin4), .pin5(1'b0), .pin7(1'b0),
    .pin9(1'b0), .pin11(1'b0), .pin13(1'b0), .pin14(1'b1));  // open: pin6, pin8, pin10, pin12
  _7408 _7408_1 (
    .pin1(_7404_1_pin2), .pin2(_7404_1_pin4), .pin3(_7408_1_pin3), .pin4(_7408_1_pin3), .pin5(BIT1),
    .pin6(_7408_1_pin6), .pin7(1'b0), .pin8(_7408_1_pin8), .pin9(BIT0), .pin10(_7408_1_pin10),
    .pin11(_7408_1_pin10), .pin12(_7404_1_pin4), .pin13(_7404_1_pin2), .pin14(1'b1));
  _7408 _7408_2 (
    .pin1(_7404_1_pin2), .pin2(S1_2), .pin3(_7408_2_pin3), .pin4(_7408_2_pin3), .pin5(BIT1),
    .pin6(_7408_2_pin6), .pin7(1'b0), .pin8(_7408_2_pin8), .pin9(BIT0), .pin10(_7408_2_pin10),
    .pin11(_7408_2_pin10), .pin12(S1_2), .pin13(_7404_1_pin2), .pin14(1'b1));
  _7408 _7408_3 (
    .pin1(S0_2), .pin2(_7404_1_pin4), .pin3(_7408_3_pin3), .pin4(_7408_3_pin3), .pin5(BIT1),
    .pin6(_7408_3_pin6), .pin7(1'b0), .pin8(_7408_3_pin8), .pin9(BIT0), .pin10(_7408_3_pin10),
    .pin11(_7408_3_pin10), .pin12(_7404_1_pin4), .pin13(S0_2), .pin14(1'b1));
  _7408 _7408_4 (
    .pin1(S0_2), .pin2(S1_2), .pin3(_7408_4_pin3), .pin4(_7408_4_pin3), .pin5(BIT1), .pin6(_7408_4_pin6),
    .pin7(1'b0), .pin8(_7408_4_pin8), .pin9(BIT0), .pin10(_7408_4_pin10), .pin11(_7408_4_pin10),
    .pin12(S1_2), .pin13(S0_2), .pin14(1'b1));
  LED A0_2 (.in(_7408_1_pin8));
  LED A2 (.in(_7408_1_pin6));
  LED B0_2 (.in(_7408_2_pin8));
  LED B1_2 (.in(_7408_2_pin6));
  LED C0_2 (.in(_7408_3_pin8));
  LED C1_2 (.in(_7408_3_pin6));
  LED D0_2 (.in(_7408_4_pin8));
  LED D1_2 (.in(_7408_4_pin6));
endmodule
